# Fritzing sketch connecting_esp (saved by Fritzing 0.9.4)
breadboards: 1

parts:
  Part1 = Arduino Uno (Rev3) - ICSP
  U2 = ESP8266 WiFi Module [part_number=ESP8266]
  U3 = V_REG_LD1117VXX [package=78xxl]
  R1 = Resistor [tolerance=±5% resistance=1k package="0402 [SMD]"]
  R2 = Resistor [tolerance=±5% resistance=2.2k package="0402 [SMD]"]

nets:
  GND: Part1.GND, Part1.RESET, U2.GPIO_0, U2.GND, U3.GND, R2.Pin_1
  N1: Part1.D0/RX, U2.RXD
  N2: Part1.D1/TX, R1.Pin_0
  N3: Part1.5V, U3.IN
  N4: U2.VCC, U2.CH_PD, U3.OUT
  N5: U2.TXD, R1.Pin_1, R2.Pin_0

custom parts:
  ESP8266 WiFi Module: Generic WiFi Module based on the ESP8266 with onboard PCB antenna and UART communications
